// Logisim project nand2tetris.circ as structural Verilog
module ALU_16bit (
  input  [15:0] InputX,
  input  ZX,
  input  NX,
  input  [15:0] InputY,
  input  ZY,
  input  NY
);
endmodule
